# Fritzing sketch fire fighting robot circuit (saved by Fritzing 0.9.10b)

parts:
  Part1 = Arduino Uno (Rev3)
  M1 = gear-motor
  M2 = gear-motor
  M3 = gear-motor
  M4 = gear-motor
  Mod1 = KY-019 5V Relay Module [package="Breakout board"]
  L298N1 = L298N DC motor driver
  M6 = RioRand LM2596
  Part2 = Bluetooth HC-05 Macho
  S1 = KY-026
  WATER_PUMP1 = water pump/motor
  S2 = KY-026
  S3 = KY-026
  VCC1 = Battery  # not connected
  M5 = Dagu DGServo 9g (Top view) [part_number=RS001B]
  Mod2 = MQ-7 breakout

nets:
  N1: Part1.D8, S1.pin4
  N2: Part1.D9_PWM, S2.pin4
  N3: Part1.D10_PWM/SS, S3.pin1
  N4: Part1.D11_PWM/MOSI, Mod2.DO
  N5: Part1.D12/MISO, Mod1.S
  N6: Part1.D2, Part2.TXD
  N7: Part1.D3_PWM, Part2.RXD
  N8: Part1.D4, L298N1.IN4
  N9: Part1.D5_PWM, L298N1.IN3
  N10: Part1.D6_PWM, L298N1.IN2
  N11: Part1.D7, L298N1.IN1
  5V: Part1.5V, M5.vcc
  GND: Part1.GND, M5.gnd
  VIN: Part1.VIN, L298N1.5V
  N12: M1.pin_1, M3.pin_1, L298N1.OUT2
  N13: M1.pin_2, M3.pin_2, L298N1.OUT1
  N14: M2.pin_1, M4.pin_1, L298N1.OUT4
  N15: M2.pin_2, M4.pin_2, L298N1.OUT3
  N16: Mod1.NO, WATER_PUMP1.pin_2
  N17: L298N1.12V, M6.Pin_3
  N18: L298N1.GND, M6.Pin_4

custom parts:
  KY-019 5V Relay Module: KY-019 5V Relay module, used to control AC circuits. (Special thanks to vanepp for fixing the PCB holes and other errors)
  L298N DC motor driver: 2x DC motor driver with 78M05 positive voltage regulator (7..35 V) L298N: max 46 V, 2 A Set 5 V Enable jumper to enable 5 V regultor (needed for the L298N) and +5 V output at screw terminal or supply external +5 V at screw terminal Set ENA and/or ENB to +5 V to enable motor permanently or supply ENA and/or ENB with PWM signal IN1 and IN2 set rotation directory for motor A (OUT1/OUT2) IN2 and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
  KY-026: ky-026 flame sensor module
  water pump/motor: WATER PUMP BY ARDUBLOCKTR
  MQ-7 breakout: MQ-5 gas sensor
